# Fritzing sketch light theremin (saved by Fritzing 0.9.2b)
breadboards: 1

parts:
  Part1 = Arduino Uno (Rev3)
  J1 = Piezo Speaker
  R1 = PHOTOCELL [package=photocell]
  R2 = Resistor [tolerance=±5% resistance=220 package="2512 [SMD]"]
  LED1 = LEDs [package=led10mm]
  R3 = Resistor [tolerance=±5% resistance=220 package="2512 [SMD]"]

nets:
  N1: Part1.A0, R1.P$2, R2.Pin_0
  N2: Part1.D3_PWM, J1.pin2
  N3: Part1.5V, R1.P$1
  N4: Part1.GND, J1.pin1, R2.Pin_1, R3.Pin_1
  N5: LED1.C, R3.Pin_0
